# Fritzing sketch PCB final design (saved by Fritzing 1.0.5)
circuit board: 8.48146cm x 6.81871cm
breadboards: 1

parts:
  J1 = JST-VHR-3N [part_number=JST-VHR-3N package=THT]
  J2 = JST-VHR-3N [part_number=JST-VHR-3N package=THT]
  J3 = JST-VHR-3N [part_number=JST-VHR-3N package=THT]
  J4 = JST-VHR-3N [part_number=JST-VHR-3N package=THT]
  J5 = JST-VHR-3N [part_number=JST-VHR-3N package=THT]
  J6 = JST-VHR-3N [part_number=JST-VHR-3N package=THT]
  J7 = JST-VHR-3N [part_number=JST-VHR-3N package=THT]
  J8 = JST-VHR-3N [part_number=JST-VHR-3N package=THT]
  J9 = JST-VHR-3N [part_number=JST-VHR-3N package=THT]
  J10 = JST-VHR-3N [part_number=JST-VHR-3N package=THT]
  VR1 = LM2596 (TO263) [part_number=LM2596 package=TO263]
  J11 = Screw terminal - 2 pins [package=THT]
  JP1 = Header 1 [package=snap-male]
  JP2 = Header 1 [package=snap-male]
  JP3 = Header 1 [package=snap-male]
  JP4 = Header 1 [package=snap-male]
  JP5 = Header 1 [package=snap-male]
  JP6 = Header 1 [package=snap-male]
  JP7 = Header 1 [package=snap-male]
  JP8 = Header 1 [package=snap-male]
  JP9 = Header 1 [package=snap-male]
  JP10 = Header 1 [package=snap-male]
  JP11 = Header 1 [package=smtso-256-et]  # not connected
  JP13 = Header 1 [package=smtso-256-et]  # not connected
  JP15 = Header 1 [package=smtso-256-et]  # not connected
  JP17 = Header 1 [package=smtso-256-et]

nets:
  N1: J1.pin2, J1.pin_5, J2.pin2, J2.pin_5, J3.pin2, J3.pin_5, J4.pin2, J4.pin_5, J5.pin2, J6.pin2, J6.pin_5, J7.pin2, J7.pin_5, J8.pin2, J8.pin_5, J9.pin2, J9.pin_5, J10.pin2, J10.pin_5, VR1.Pin_2
  N2: J1.pin1, J1.pin_4, J2.pin1, J2.pin_4, J3.pin1, J3.pin_4, J4.pin1, J4.pin_4, J5.pin1, J6.pin1, J6.pin_4, J7.pin1, J7.pin_4, J8.pin1, J8.pin_4, J9.pin1, J9.pin_4, J10.pin1, J10.pin_4, VR1.Pin_3, VR1.Tab, J11.pin1, JP17.1
  N3: J1.pin3, J1.pin_6, JP1.1
  N4: J2.pin3, J2.pin_6, JP2.1
  N5: J3.pin3, J3.pin_6, JP3.1
  N6: J4.pin3, J4.pin_6, JP4.1
  N7: J5.pin3, J5.pin_6, JP5.1
  N8: J6.pin3, J6.pin_6, JP6.1
  N9: J7.pin3, J7.pin_6, JP7.1
  N10: J8.pin3, J8.pin_6, JP8.1
  N11: J9.pin3, J9.pin_6, JP9.1
  N12: J10.pin3, J10.pin_6, JP10.1
  N13: VR1.Pin_1, J11.pin2
